# Fritzing sketch Matrix Clock (saved by Fritzing 0.9.10b)
breadboards: 1

parts:
  8x8_LED_Modul_mit_MAX2 = 8x8 LED Modul mit MAX7219 [package=THT]
  8x8_LED_Modul_mit_MAX1 = 8x8 LED Modul mit MAX7219 [package=THT]
  8x8_LED_Modul_mit_MAX3 = 8x8 LED Modul mit MAX7219 [package=THT]
  8x8_LED_Modul_mit_MAX4 = 8x8 LED Modul mit MAX7219 [package=THT]
  R1 = Resistor [tolerance=±5% power=0.25 resistance=10k package=THT]
  S1 = Momentary Switch [package=ksa_sealed_tac_switch]
  RHT1 = Humidity and Temperature Sensor RHT03
  R2 = Resistor [tolerance=±5% power=0.25 resistance=10k package=THT]
  Pico_H1 = Raspberry Pi Pico H

nets:
  N1: 8x8_LED_Modul_mit_MAX2.VCC_Eingang, 8x8_LED_Modul_mit_MAX1.VCC_Ausgang
  N2: 8x8_LED_Modul_mit_MAX2.GND_Eingang, 8x8_LED_Modul_mit_MAX1.GND_Ausgang
  N3: 8x8_LED_Modul_mit_MAX2.DIN_Eingang, 8x8_LED_Modul_mit_MAX1.DOUT_Ausgang
  N4: 8x8_LED_Modul_mit_MAX2.CS_Eingang, 8x8_LED_Modul_mit_MAX1.CS_Ausgang
  N5: 8x8_LED_Modul_mit_MAX2.CLK_Eingang, 8x8_LED_Modul_mit_MAX1.CLK_Ausgang
  N6: 8x8_LED_Modul_mit_MAX2.VCC_Ausgang, 8x8_LED_Modul_mit_MAX3.VCC_Eingang
  N7: 8x8_LED_Modul_mit_MAX2.GND_Ausgang, 8x8_LED_Modul_mit_MAX3.GND_Eingang
  N8: 8x8_LED_Modul_mit_MAX2.DOUT_Ausgang, 8x8_LED_Modul_mit_MAX3.DIN_Eingang
  N9: 8x8_LED_Modul_mit_MAX2.CS_Ausgang, 8x8_LED_Modul_mit_MAX3.CS_Eingang
  N10: 8x8_LED_Modul_mit_MAX2.CLK_Ausgang, 8x8_LED_Modul_mit_MAX3.CLK_Eingang
  N11: 8x8_LED_Modul_mit_MAX1.VCC_Eingang, R1.Pin_0, S1.1, RHT1.Vcc, Pico_H1.VBUS
  N12: 8x8_LED_Modul_mit_MAX1.GND_Eingang, RHT1.GND_2, R2.Pin_0, Pico_H1.GND
  N13: 8x8_LED_Modul_mit_MAX1.DIN_Eingang, Pico_H1.GP0
  N14: 8x8_LED_Modul_mit_MAX1.CS_Eingang, Pico_H1.GP1
  N15: 8x8_LED_Modul_mit_MAX1.CLK_Eingang, Pico_H1.GP2
  N16: 8x8_LED_Modul_mit_MAX3.VCC_Ausgang, 8x8_LED_Modul_mit_MAX4.VCC_Eingang
  N17: 8x8_LED_Modul_mit_MAX3.GND_Ausgang, 8x8_LED_Modul_mit_MAX4.GND_Eingang
  N18: 8x8_LED_Modul_mit_MAX3.DOUT_Ausgang, 8x8_LED_Modul_mit_MAX4.DIN_Eingang
  N19: 8x8_LED_Modul_mit_MAX3.CS_Ausgang, 8x8_LED_Modul_mit_MAX4.CS_Eingang
  N20: 8x8_LED_Modul_mit_MAX3.CLK_Ausgang, 8x8_LED_Modul_mit_MAX4.CLK_Eingang
  N21: R1.Pin_1, RHT1.Data-signal, Pico_H1.GP4
  N22: S1.4, R2.Pin_1, Pico_H1.GP3

custom parts:
  Raspberry Pi Pico H: Raspberry Pi Pico H. Based around the RP2040 microcontroller the Pico H is a low cost microcontroller device bringing Raspberry Pi quality, cost, and easy of use to the microcontroller space.
